# Fritzing sketch Circuit Diagram (saved by Fritzing 0.9.2b)

parts:
  Eleman1 = Arduino Mega 2560 (Rev3)
  J3 = Basic Servo
  J2 = Basic Servo
  J1 = Basic Servo
  Eleman2 = LCD1602-I2C
  TCS1 = TCS3200
  J4 = LOAD_CELL [package=1x03]
  Eleman3 = HX711 Weighing Sensor Module
  R1 = Resistor [tolerance=±5% resistance=1k package="2512 [SMD]"]
  R2 = Resistor [tolerance=±5% resistance=1k package="2512 [SMD]"]
  Eleman4 = Thumb Joystick
  Eleman5 = Thumb Joystick
  YwRobot_Power_Supply1 = YwRobot Breadboard Power Supply [part_number=545043]
  Bat2 = battery_holder_single_18650

nets:
  N1: Eleman1.A0, Eleman4.VERT
  N2: Eleman1.A1, Eleman4.HORZ
  N3: Eleman1.A2, Eleman5.VERT
  N4: Eleman1.A3, Eleman5.HORZ
  N5: Eleman1.D21/SCL, Eleman2.SCL
  N6: Eleman1.D20/SDA, Eleman2.SDA
  N7: Eleman1.D13_PWM, Eleman4.SEL
  N8: Eleman1.D12_PWM, Eleman5.SEL
  N9: Eleman1.D11_PWM, Eleman3.CK/TX
  N10: Eleman1.D10_PWM, Eleman3.DO/RX
  N11: Eleman1.D9_PWM, TCS1.OUT
  N12: Eleman1.D8_PWM, TCS1.S3
  N13: Eleman1.D2_PWM, J2.pulse
  N14: Eleman1.D3_PWM, J1.pulse
  N15: Eleman1.D4_PWM, J3.pulse
  N16: Eleman1.D5_PWM, TCS1.S0
  N17: Eleman1.D6_PWM, TCS1.S1
  N18: Eleman1.D7_PWM, TCS1.S2
  GND: J1.gnd, Eleman2.GND
  VCC: Eleman2.VCC, TCS1.VCC, Eleman3.VCC, YwRobot_Power_Supply1.VCC#6
  N19: J4.B, Eleman3.E-
  N20: J4.W, Eleman3.A+
  N21: J4.R, Eleman3.E+, R2.Pin_0
  N22: Eleman3.A-, R1.Pin_1
  N23: Eleman4.GND, YwRobot_Power_Supply1.GND#12
  N24: YwRobot_Power_Supply1.VCC#9, Bat2.+#1
  N25: YwRobot_Power_Supply1.GND#13, Bat2.+#0

custom parts:
  LCD1602-I2C: A standard character display, usually with 2x16 characters. Comes in many colors with LCM1602 IIC attached.
  TCS3200: COLOR SENSING TCS3200
  YwRobot Breadboard Power Supply: The YwRobot Breadboard Power Supply (MB-V2) has two power rails; they can be 5V or 3V3. Power to the module can be provided through the female USB socket or through the A10 (female) 2.1mm power jack.
  battery_holder_single_18650: single 18650 battery holder
